# Fritzing sketch multidryer (saved by Fritzing 0.9.3b)
breadboards: 1

parts:
  U1 = ESP32S-HiLetgo [part_number=ESP32S-HiLetgo]
  J1 = Piezo Speaker
  Part1 = HX711 Weighing Sensor Module
  RY1 = SSR-40VA
  RY2 = SSR-40VA
  RY3 = SSR-40VA
  tft1 = 3.5in tft touch screen
  F2 = Fan - Ventilador [package=THT]
  F3 = Fan - Ventilador [package=THT]
  A1 = 100w-ptc-air-heater
  S1 = Round Pushbutton
  PS1 = prefix0000 [part_number=S-350-60]
  F4 = FUSE [package=fuse_5mm]
  F5 = FUSE [package=fuse_5mm]
  F6 = FUSE [package=fuse_5mm]
  M1 = RioRand LM2596
  S2 = Round Pushbutton

nets:
  N1: U1.GPIO36, Part1.DO/RX
  N2: U1.GPIO32, Part1.CK/TX
  N3: U1.GPIO26, RY1.Pin_3
  N4: U1.GPIO27, RY2.Pin_3
  N5: U1.GPIO14, RY3.Pin_3
  GND: U1.GND, J1.pin2, Part1.GND, RY2.Pin_4, RY3.Pin_4
  VIN: U1.VIN, Part1.VCC, tft1.LCD_RD, M1.Pin_3
  N6: U1.GPIO19, J1.pin1
  N7: RY1.Pin_1, RY2.Pin_1, RY3.Pin_1, S1.leg1, PS1.connector8
  N8: RY1.Pin_2, F4.2
  N9: RY1.Pin_4, tft1.GND, M1.Pin_4
  N10: RY2.Pin_2, F5.2
  N11: RY3.Pin_2, F6.2
  N12: F2.5V, F5.1
  GND_2: F2.GND, F3.GND, A1.Pin_2, PS1.connector7, S2.leg1
  N13: F3.5V, F6.1
  N14: A1.Pin_1, F4.1
  N15: PS1.connector2, M1.Pin_1
  N16: PS1.connector3, M1.Pin_2

custom parts:
  ESP32S-HiLetgo: HiLetgo ESP-WROOM-32 ESP32 ESP-32S Development Board 2.4GHz Dual-Mode WiFi + Bluetooth Dual Cores Microcontroller The ESP32 integrated with Antenna switches, RF Balun, power amplifiers, low-noise amplifiers, filters, and management modules, and the entire solution occupies the least area of PCB. 2.4 GHz Wi-Fi plus Bluetooth dual-mode chip, with TSMC Ultra-low power consumption 40nm technology,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
  SSR-40VA: SSR-40VA solid state relay.
  3.5in tft touch screen: 3.2" tft touch screen lcd display
  Fan - Ventilador: Ventilador de 2 pines, se encuentra comunmente en computadoras de escritorio
  100w-ptc-air-heater: 110V 100W Surface Insulated PTC Air Heater PTC Heating Element Incubator Controller Incubation Heater.
